// Logisim project control-logic.circ as structural Verilog: 1 circuit, main circuit control_logic
module control_logic (
  input  [31:0] Instruction,
  input  BrEq,
  input  BrLt,
  output PCSel,
  output RegWEn,
  output [2:0] ImmSel,
  output BrUn,
  output ASel,
  output BSel,
  output [3:0] ALUSel,
  output MemWEn,
  output [1:0] WBSel
);

  wire add_add, addi, and_22_out, and_23_out, and_24_out, and_25_out, and_26_out, and_27_out, and_28_out,
       and_29_out, and_30_out, and_31_out, and_32_out, and_33_out, and_34_out, and_35_out, and_36_out,
       and_37_out, and_38_out, and_and, andi, fun7_00, fun7_0000000, fun7_0000001, fun7_20, fun7_0100000,
       fun_0, fun_1, fun_2, fun_3, fun_4, fun_5, fun_6, fun_7, mul_mul, mulh, mulhu, not_1_out, not_2_out,
       op_0000011, op_0010011, op_0010111, op_0110011, op_0110111, op_1100011, op_1100111, op_1101111,
       or_1_out, or_2_out, or_3_out, or_4_out, or_5_out, or_6_out, or_7_out, or_8_out, or_9_out, or_10_out,
       or_11_out, or_12_out, or_13_out, or_or, ori, sll_sll, slli, slt_slt, slti, sra_sra, srai, srl_srl,
       srli, sub_sub, WBSel_AUL, WBSel_mem, WBSel_PC, xor_xor, xori;
  wire [2:0] priority_encoder_6_out;
  wire [3:0] multiplexer_1_out, priority_encoder_2_out;
  wire [5:0] bit_extender_1_out, ROMinput, undriven;
  wire [15:0] rom_1_data;

  ROM #(.addrWidth(6), .dataWidth(16)) rom_1 (.addr(undriven), .data(rom_1_data));
  Priority_Encoder priority_encoder_1 (
    .in0(op_0000011), .in1(op_0010011), .in2(op_0110011), .in3(op_0010111), .in5(op_0110111),
    .in6(op_1100111), .in7(op_1101111), .gs(RegWEn));  // open: in4, out, en_in, en_out
  or or_1 (or_1_out, add_add, addi);
  or or_2 (or_2_out, sll_sll, slli);
  or or_3 (or_3_out, slt_slt, slti);
  or or_4 (or_4_out, xor_xor, xori);
  or or_5 (or_5_out, srl_srl, srli);
  or or_6 (or_6_out, or_or, ori);
  or or_7 (or_7_out, and_and, andi);
  or or_8 (or_8_out, sra_sra, srai);
  and and_1 (add_add, op_0110011, fun7_0000000, fun_0);
  and and_2 (mul_mul, op_0110011, fun7_0000001, fun_0);
  and and_3 (sub_sub, op_0110011, fun7_0100000, fun_0);
  and and_4 (sll_sll, op_0110011, fun7_0000000, fun_1);
  and and_5 (mulh, op_0110011, fun7_0000001, fun_1);
  and and_6 (mulhu, op_0110011, fun7_0000001, fun_3);
  and and_7 (slt_slt, op_0110011, fun7_0000000, fun_4);
  and and_8 (xor_xor, op_0110011, fun7_0000000, fun_4);
  and and_9 (srl_srl, op_0110011, fun7_0000000, fun_5);
  and and_10 (sra_sra, op_0110011, fun7_0100000, fun_5);
  and and_11 (or_or, op_0110011, fun7_0000000, fun_6);
  and and_12 (and_and, op_0110011, fun7_0000000, fun_7);
  Priority_Encoder #(.select_enc(4)) priority_encoder_2 (
    .in0(or_1_out), .in1(or_2_out), .in2(or_3_out), .in4(or_4_out), .in5(or_5_out), .in6(or_6_out),
    .in7(or_7_out), .in8(mul_mul), .in9(mulh), .in11(mulhu), .in12(sub_sub), .in13(or_8_out),
    .out(priority_encoder_2_out));  // open: in3, in10, in14, in15, gs, en_out, en_in
  Multiplexer #(.width(4)) multiplexer_1 (
    .in0(4'b0000), .in1(priority_encoder_2_out), .out(multiplexer_1_out), .sel(or_9_out));
  or or_9 (or_9_out, op_0010011, op_0110011);
  or or_10 (or_10_out, op_0110011, op_1100111, op_0010011, op_0000011);
  or or_11 (or_11_out, op_0010111, op_0110111);
  Multiplexer #(.width(4)) multiplexer_2 (.in0(multiplexer_1_out), .in1(4'b1111), .out(ALUSel), .sel(op_0110111));
  and and_13 (addi, op_0010011, fun_0);
  and and_14 (slli, op_0010011, fun7_0000000, fun_1);
  and and_15 (slti, op_0010011, fun_2);
  and and_16 (xori, op_0010011, fun_4);
  and and_17 (srli, op_0010011, fun7_0000000, fun_5);
  and and_18 (srai, op_0010011, fun7_0100000, fun_5);
  and and_19 (ori, op_0010011, fun_6);
  and and_20 (andi, op_0010011, fun_7);
  Priority_Encoder priority_encoder_3 (
    .in0(or_10_out), .in1(MemWEn), .in2(op_1100011), .in3(or_11_out), .in4(op_1101111), .out(ImmSel));  // open: in5, in6, in7, en_in, gs, en_out
  or or_12 (or_12_out, fun_6, fun_7);
  not not_1 (not_1_out, BrEq);
  Comparator #(.width(7)) comparator_1 (.a(Instruction[6:0]), .b(7'b0000011), .eq(op_0000011));  // open: gt, lt
  Comparator #(.width(7)) comparator_2 (.a(Instruction[6:0]), .b(7'b0010011), .eq(op_0010011));  // open: gt, lt
  Comparator #(.width(7)) comparator_3 (.a(Instruction[6:0]), .b(7'b0110011), .eq(op_0110011));  // open: gt, lt
  Comparator #(.width(7)) comparator_4 (.a(Instruction[6:0]), .b(7'b1100011), .eq(op_1100011));  // open: gt, lt
  and and_21 (BrUn, op_1100011, or_12_out);
  and and_22 (and_22_out, fun_0, op_1100011, BrEq);
  and and_23 (and_23_out, fun_1, op_1100011, not_1_out);
  and and_24 (and_24_out, fun_4, op_1100011, BrLt);
  and and_25 (and_25_out, BrLt, op_1100011, fun_6);
  and and_26 (and_26_out, fun_5, op_1100011, not_2_out);
  not not_2 (not_2_out, BrLt);
  and and_27 (and_27_out, BrLt, op_1100011, fun_7);
  and and_28 (and_28_out, op_1100111, fun_0);
  or or_13 (or_13_out, op_1101111, op_0010111);
  Priority_Encoder priority_encoder_4 (
    .in0(and_22_out), .in1(and_23_out), .in2(and_24_out), .in3(and_25_out), .in4(and_26_out),
    .in5(and_27_out), .in6(and_28_out), .in7(or_13_out), .gs(PCSel));  // open: out, en_in, en_out
  Comparator #(.width(7)) comparator_5 (.a(Instruction[6:0]), .b(7'b0100011), .eq(MemWEn));  // open: gt, lt
  Comparator #(.width(7)) comparator_6 (.a(Instruction[6:0]), .b(7'b0010111), .eq(op_0010111));  // open: gt, lt
  Comparator #(.width(7)) comparator_7 (.a(Instruction[6:0]), .b(7'b0110111), .eq(op_0110111));  // open: gt, lt
  Comparator #(.width(7)) comparator_8 (.a(Instruction[6:0]), .b(7'b1101111), .eq(op_1101111));  // open: gt, lt
  Comparator #(.width(7)) comparator_9 (.a(Instruction[6:0]), .b(7'b1100111), .eq(op_1100111));  // open: gt, lt
  or or_14 (WBSel_PC, MemWEn, op_0000011, op_1100011);
  or or_15 (WBSel_AUL, op_0010011, op_0110011, op_0010111, op_0110111);
  or or_16 (WBSel_mem, op_1101111, op_1100111);
  or or_17 (ASel, op_1100011, op_0010111, op_1101111);
  Priority_Encoder #(.select_enc(2)) priority_encoder_5 (
    .in0(WBSel_PC), .in1(WBSel_AUL), .in2(WBSel_mem), .out(WBSel));  // open: in3, gs, en_out, en_in
  Comparator #(.width(3)) comparator_10 (.a(Instruction[14:12]), .b(3'b000), .eq(fun_0));  // open: gt, lt
  Comparator #(.width(3)) comparator_11 (.a(Instruction[14:12]), .b(3'b001), .eq(fun_1));  // open: gt, lt
  Comparator #(.width(3)) comparator_12 (.a(Instruction[14:12]), .b(3'b010), .eq(fun_2));  // open: gt, lt
  Comparator #(.width(3)) comparator_13 (.a(Instruction[14:12]), .b(3'b011), .eq(fun_3));  // open: gt, lt
  Comparator #(.width(3)) comparator_14 (.a(Instruction[14:12]), .b(3'b100), .eq(fun_4));  // open: gt, lt
  Comparator #(.width(3)) comparator_15 (.a(Instruction[14:12]), .b(3'b101), .eq(fun_5));  // open: gt, lt
  Comparator #(.width(3)) comparator_16 (.a(Instruction[14:12]), .b(3'b110), .eq(fun_6));  // open: gt, lt
  Comparator #(.width(3)) comparator_17 (.a(Instruction[14:12]), .b(3'b111), .eq(fun_7));  // open: gt, lt
  or or_18 (BSel, MemWEn, op_0000011, op_0010011, op_1100011, op_0010111, op_0110111, op_1101111, op_1100111);
  Comparator #(.width(7)) comparator_18 (.a(Instruction[31:25]), .b({7{1'b0}}), .eq(fun7_0000000));  // open: gt, lt
  Comparator #(.width(7)) comparator_19 (.a(Instruction[31:25]), .b(7'b0000001), .eq(fun7_0000001));  // open: gt, lt
  Comparator #(.width(7)) comparator_20 (.a(Instruction[31:25]), .b(7'b0100000), .eq(fun7_0100000));  // open: gt, lt
  and and_29 (and_29_out, op_0010011, fun_0);
  and and_30 (and_30_out, op_0010011, fun_1);
  and and_31 (and_31_out, op_0010011, fun_2);
  and and_32 (and_32_out, op_0010011, fun_4);
  and and_33 (and_33_out, op_0010011, fun_5);
  and and_34 (and_34_out, op_0010011, fun_6);
  and and_35 (and_35_out, op_0010011, fun_7);
  and and_36 (and_36_out, and_30_out, fun7_00);
  and and_37 (and_37_out, fun7_00, and_33_out);
  and and_38 (and_38_out, and_33_out, fun7_20);
  Priority_Encoder priority_encoder_6 (
    .in0(and_29_out), .in1(and_36_out), .in2(and_31_out), .in3(and_32_out), .in4(and_37_out),
    .in5(and_38_out), .in6(and_34_out), .in7(and_35_out), .out(priority_encoder_6_out));  // open: en_in, gs, en_out
  assign bit_extender_1_out = {{3{priority_encoder_6_out[2]}}, priority_encoder_6_out};  // Bit_Extender bit_extender_1
  Adder #(.width(6)) adder_1 (.a(bit_extender_1_out), .b({6{1'b1}}), .out(ROMinput));  // open: cin, cout

  // Other names for the same wires on the sheet: op_0100011 = MemWEn; opcode[6:0] = Instruction[6:0];
  //   rd[4:0] = Instruction[11:7]; funct3[2:0] = Instruction[14:12]; rs1[4:0] = Instruction[19:15];
  //   rs2[4:0] = Instruction[24:20]; funct7[6:0] = Instruction[31:25]

  // Notes on the sheet:
  //   lui
  //   INPUTS to your circuit
  //   Connect ROM Input here ->
  //   I-type
  //   r-type
  //   auipc
  //   jalr
  //   jal
  //   ALUSel
  //   RegWEn   一般有rd的都要为1
  //   R-type
  //   contents of rom_1 (hex, n*v repeats v):
  //   100 14*0 1041 10c1 1141 1241 12c1 16c1 1341 13c1
  //   ROM FOR CONTROL LOGIC
  //   DON'T CHANGE THE LOCATIONS OF THE INPUTS AND OUTPUTS!
  //   This is only if you choose to do the ROM option
  //   CONNECT
  //   WIRE
  //   TO
  //   USE
  //   ROM
  //   OUTPUT from your circuit
  //   R-type
  //   JI-type
  //   I-type
  //   S-type
  //   B-type
  //   U-type
  //   J-type
  //   I-type
  //   Immsel
  //   Reminder: If using ROM, use combinational logic for PCSel
  //   BrUn
  //   MemWEn
  //   PCSel
  //   I-type
  //   R-type
  //   B-type
  //   S-type
  //   U-type
  //   J-type
  //   JI-type
  //   S
  //   Iw
  //   B
  //   I
  //   R
  //   auipc
  //   lui
  //   jal
  //   jalr
  //   ASel
  //   WBSel
  //   FUNCT3
  //   BSel
  //   FUNCT7
endmodule
