// Logisim project cpu.circ as structural Verilog: 1 circuit, main circuit cpu
module cpu (
  input  clk,
  input  [31:0] Instruction,
  input  [31:0] MemReadData,
  output [31:0] MemAddress,
  output [31:0] ProgramCounter,
  output [31:0] ra,
  output [31:0] sp,
  output [31:0] t0,
  output [31:0] t1,
  output [31:0] t2,
  output [31:0] s0,
  output [31:0] s1,
  output [31:0] a0,
  output [3:0] MemWriteMask,
  output [31:0] MemWriteData
);

  wire ASel, BrEq, BrLt, BrUn, BSel, MemWEn, PCSel, RegWEn;
  wire [1:0] WBSel;
  wire [2:0] funct3, ImmSel;
  wire [3:0] ALUSel;
  wire [6:0] funct7;
  wire [24:0] Instruction2;
  wire [31:0] imm, Mem, multiplexer_1_out, multiplexer_2_out, multiplexer_3_out, multiplexer_4_out, PC_4,
       ProgramCounter2, RDrs1, RDrs2, WBResult;

  Adder #(.width(32)) adder_1 (.a(ProgramCounter), .b(32'h4), .out(PC_4));  // open: cin, cout
  Multiplexer #(.width(32)) multiplexer_1 (.in0(PC_4), .in1(MemAddress), .out(multiplexer_1_out), .sel(PCSel));
  Multiplexer #(.width(32)) multiplexer_2 (.in0(Instruction), .in1(32'h13), .out(multiplexer_2_out), .sel(PCSel));
  Register #(.width(32)) PC (.D(multiplexer_1_out), .clk(clk), .Q(ProgramCounter));  // open: en, clr
  Register #(.width(32)) register_1 (.D(ProgramCounter), .clk(clk), .Q(ProgramCounter2));  // open: en, clr
  Register #(.width(32)) register_2 (
    .D(multiplexer_2_out), .clk(clk), .Q({funct7, Instruction2[24:15], funct3, Instruction2[11:0]}));  // open: en, clr
  control_logic control_logic_1 (
    .Instruction({funct7, Instruction2[24:15], funct3, Instruction2[11:0]}), .BrEq(BrEq), .BrLt(BrLt),
    .PCSel(PCSel), .RegWEn(RegWEn), .ImmSel(ImmSel), .BrUn(BrUn), .ASel(ASel), .BSel(BSel), .ALUSel(ALUSel),
    .MemWEn(MemWEn), .WBSel(WBSel));
  regfile regfile_1 (
    .ReadIndex1(Instruction2[19:15]), .ReadIndex2(Instruction2[24:20]), .WriteIndex(Instruction2[11:7]),
    .WriteData(WBResult), .RegWEn(RegWEn), .clk(clk), .ra(ra), .sp(sp), .t0(t0), .t1(t1), .t2(t2), .s0(s0),
    .s1(s1), .a0(a0), .ReadData1(RDrs1), .ReadData2(RDrs2));
  imm_gen imm_gen_1 (
    .Instruction({funct7, Instruction2[24:15], funct3, Instruction2[11:0]}), .ImmSel(ImmSel), .Immediate(imm));
  Multiplexer #(.width(32)) multiplexer_3 (.in0(RDrs1), .in1(ProgramCounter2), .out(multiplexer_3_out), .sel(ASel));
  Multiplexer #(.width(32)) multiplexer_4 (.in0(RDrs2), .in1(imm), .out(multiplexer_4_out), .sel(BSel));
  alu alu_1 (.A(multiplexer_3_out), .B(multiplexer_4_out), .ALUSel(ALUSel), .ALUResult(MemAddress));
  branch_comp branch_comp_1 (.BrData1(RDrs1), .BrData2(RDrs2), .BrUn(BrUn), .BrEq(BrEq), .BrLt(BrLt));
  partial_store partial_store_1 (
    .Instruction({funct7, Instruction2[24:15], funct3, Instruction2[11:0]}), .MemAddress(MemAddress),
    .DataFromReg(RDrs2), .MemWEn(MemWEn), .MemWriteMask(MemWriteMask), .DataToMem(MemWriteData));
  partial_load partial_load_1 (
    .Instruction({funct7, Instruction2[24:15], funct3, Instruction2[11:0]}), .MemAddress(MemAddress),
    .DataFromMem(MemReadData), .DataToReg(Mem));
  Multiplexer #(.select(2), .width(32)) multiplexer_5 (
    .in0(Mem), .in1(MemAddress), .in2(PC_4), .out(WBResult), .sel(WBSel));  // open: in3

  // Other names for the same wires on the sheet: ALURes[31:0] = MemAddress; opcode[6:0] = Instruction2[6:0];
  //   rd[4:0] = Instruction2[11:7]; Instruction2 (some bits) = {funct7, funct3}; rs1[4:0] = Instruction2[19:15];
  //   rs2[4:0] = Instruction2[24:20]

  // Notes on the sheet:
  //   Instruction Splitter 
  //   To IMEM
  //   IMEM (do **NOT** move this)
  //   From IMEM
  //   It is OK to move the PC, RegFile, ALU, MEM, Branch Comp, Imm Gen, Partial Load, Partial Store and Control Logic to wherever is most convenient for you when constructing your CPU, and to delete this text
  //   Inputs/Outputs for testing. Do **NOT** move these.
  //   To DMEM
  //   DMEM (do **NOT** move this)
  //   From DMEM
endmodule
