// Logisim project imm-gen.circ as structural Verilog: 1 circuit, main circuit imm_gen
module imm_gen (
  input  [31:0] Instruction,
  input  [2:0] ImmSel,
  output [31:0] Immediate
);

  wire [31:0] Btype, Itype, Jtype, Stype;

  assign Itype = {{20{Instruction[31]}}, Instruction[31:20]};  // Bit_Extender bit_extender_1
  assign Stype = {{20{Instruction[31]}}, {Instruction[31:25], Instruction[11:7]}};  // Bit_Extender bit_extender_2
  assign Btype = {{19{Instruction[31]}}, {Instruction[31], Instruction[7], Instruction[30:25], Instruction[11:8], 1'b0}};  // Bit_Extender bit_extender_3
  assign Jtype = {{11{Instruction[31]}}, {Instruction[31], Instruction[19:12], Instruction[20], Instruction[30:21], 1'b0}};  // Bit_Extender bit_extender_4
  Multiplexer #(.select(3), .width(32)) multiplexer_1 (
    .in0(Itype), .in1(Stype), .in2(Btype), .in3({Instruction[31:12], {12{1'b0}}}), .in4(Jtype),
    .out(Immediate), .sel(ImmSel));  // open: in5, in6, in7

  // Other names for the same wires on the sheet: inst_11_8[3:0] = Instruction[11:8]; inst_7 = Instruction[7];
  //   inst_24_21[3:0] = Instruction[24:21]; Utype[31:12] = Instruction[31:12]; inst_30_25[5:0] = Instruction[30:25];
  //   inst_20 = Instruction[20]; inst_19_12[7:0] = Instruction[19:12]; inst_31 = Instruction[31];
  //   inst_0_6[6:0] = Instruction[6:0]

  // Notes on the sheet:
  //   INPUTS to your circuit
  //   DON'T CHANGE THE LOCATIONS OF THE INPUTS AND OUTPUTS!
  //   OUTPUT from your circuit
endmodule
