// Logisim project partial-load.circ as structural Verilog: 1 circuit, main circuit partial_load
module partial_load (
  input  [31:0] Instruction,
  input  [31:0] MemAddress,
  input  [31:0] DataFromMem,
  output [31:0] DataToReg
);

  wire and_1_out, and_2_out, and_3_out, and_4_out, and_5_out, and_6_out, and_7_out, and_8_out, lb, lh, load,
       lw, Ob00, Ob01, Ob10, Ob11;
  wire [2:0] SignExt;
  wire [31:0] bit_extender_1_out, bit_extender_2_out, bit_extender_3_out, bit_extender_4_out,
       bit_extender_5_out, bit_extender_6_out, bit_extender_7_out;

  Comparator #(.width(7)) comparator_1 (.a(Instruction[6:0]), .b(7'b0000011), .eq(load));  // open: gt, lt
  Comparator #(.width(3)) comparator_2 (.a(Instruction[14:12]), .b(3'b000), .eq(lb));  // open: gt, lt
  Comparator #(.width(3)) comparator_3 (.a(Instruction[14:12]), .b(3'b001), .eq(lh));  // open: gt, lt
  Comparator #(.width(3)) comparator_4 (.a(Instruction[14:12]), .b(3'b010), .eq(lw));  // open: gt, lt
  assign bit_extender_1_out = {{24{DataFromMem[7]}}, DataFromMem[7:0]};  // Bit_Extender bit_extender_1
  assign bit_extender_2_out = {{24{DataFromMem[15]}}, DataFromMem[15:8]};  // Bit_Extender bit_extender_2
  assign bit_extender_3_out = {{24{DataFromMem[23]}}, DataFromMem[23:16]};  // Bit_Extender bit_extender_3
  assign bit_extender_4_out = {{24{DataFromMem[31]}}, DataFromMem[31:24]};  // Bit_Extender bit_extender_4
  assign bit_extender_5_out = {{16{DataFromMem[15]}}, DataFromMem[15:0]};  // Bit_Extender bit_extender_5
  assign bit_extender_6_out = {{16{DataFromMem[23]}}, DataFromMem[23:8]};  // Bit_Extender bit_extender_6
  assign bit_extender_7_out = {{16{DataFromMem[31]}}, DataFromMem[31:16]};  // Bit_Extender bit_extender_7
  Multiplexer #(.select(3), .width(32)) multiplexer_1 (
    .in0(bit_extender_1_out), .in1(bit_extender_2_out), .in2(bit_extender_3_out), .in3(bit_extender_4_out),
    .in4(bit_extender_5_out), .in5(bit_extender_6_out), .in6(bit_extender_7_out), .in7(DataFromMem),
    .out(DataToReg), .sel(SignExt));
  Comparator #(.width(2)) comparator_5 (.a(MemAddress[1:0]), .b(2'b00), .eq(Ob00));  // open: gt, lt
  Comparator #(.width(2)) comparator_6 (.a(MemAddress[1:0]), .b(2'b01), .eq(Ob01));  // open: gt, lt
  Comparator #(.width(2)) comparator_7 (.a(MemAddress[1:0]), .b(2'b10), .eq(Ob10));  // open: gt, lt
  Comparator #(.width(2)) comparator_8 (.a(MemAddress[1:0]), .b(2'b11), .eq(Ob11));  // open: gt, lt
  and and_1 (and_1_out, load, lb, Ob00);
  and and_2 (and_2_out, load, lb, Ob01);
  and and_3 (and_3_out, load, lb, Ob10);
  and and_4 (and_4_out, load, lb, Ob11);
  and and_5 (and_5_out, load, lh, Ob00);
  and and_6 (and_6_out, load, lh, Ob01);
  and and_7 (and_7_out, load, lh, Ob10);
  and and_8 (and_8_out, load, lw, Ob00);
  Priority_Encoder priority_encoder_1 (
    .in0(and_1_out), .in1(and_2_out), .in2(and_3_out), .in3(and_4_out), .in4(and_5_out), .in5(and_6_out),
    .in6(and_7_out), .in7(and_8_out), .out(SignExt));  // open: en_in, gs, en_out

  // Other names for the same wires on the sheet: DataFromMem7_0[7:0] = DataFromMem[7:0];
  //   DataFromMem15_0[15:0] = DataFromMem[15:0]; DataFromMem15_8[7:0] = DataFromMem[15:8];
  //   DataFromMem23_8[15:0] = DataFromMem[23:8]; DataFromMem23_16[7:0] = DataFromMem[23:16];
  //   DataFromMem31_16[15:0] = DataFromMem[31:16]; DataFromMem31_24[7:0] = DataFromMem[31:24];
  //   opcode[6:0] = Instruction[6:0]; funct3[2:0] = Instruction[14:12]; Obxx[1:0] = MemAddress[1:0]

  // Notes on the sheet:
  //   INPUTS to your circuit
  //   DON'T CHANGE THE LOCATIONS OF THE INPUTS AND OUTPUTS!
  //   OUTPUT from your circuit
endmodule
