// Logisim project partial-store.circ as structural Verilog: 1 circuit, main circuit partial_store
module partial_store (
  input  [31:0] Instruction,
  input  [31:0] MemAddress,
  input  [31:0] DataFromReg,
  input  MemWEn,
  output [3:0] MemWriteMask,
  output [31:0] DataToMem
);

  wire and_1_out, and_2_out, and_3_out, and_4_out, and_5_out, and_6_out, and_7_out, Ob00, Ob01, Ob10, Ob11,
       sb, sh, sw;
  wire [2:0] index;
  wire [3:0] multiplexer_2_out;

  Comparator #(.width(3)) comparator_1 (.a(Instruction[14:12]), .b(3'b000), .eq(sb));  // open: gt, lt
  Comparator #(.width(3)) comparator_2 (.a(Instruction[14:12]), .b(3'b001), .eq(sh));  // open: gt, lt
  Comparator #(.width(3)) comparator_3 (.a(Instruction[14:12]), .b(3'b010), .eq(sw));  // open: gt, lt
  and and_1 (and_1_out, sb, Ob00);
  and and_2 (and_2_out, sb, Ob01);
  and and_3 (and_3_out, sb, Ob10);
  and and_4 (and_4_out, sb, Ob11);
  and and_5 (and_5_out, sh, Ob00);
  and and_6 (and_6_out, sh, Ob10);
  and and_7 (and_7_out, sw, Ob00);
  Priority_Encoder priority_encoder_1 (
    .in0(and_1_out), .in1(and_2_out), .in2(and_3_out), .in3(and_4_out), .in4(and_5_out), .in5(and_6_out),
    .in6(and_7_out), .out(index));  // open: in7, en_in, gs, en_out
  Comparator #(.width(2)) comparator_4 (.a(MemAddress[1:0]), .b(2'b00), .eq(Ob00));  // open: gt, lt
  Comparator #(.width(2)) comparator_5 (.a(MemAddress[1:0]), .b(2'b01), .eq(Ob01));  // open: gt, lt
  Comparator #(.width(2)) comparator_6 (.a(MemAddress[1:0]), .b(2'b10), .eq(Ob10));  // open: gt, lt
  Comparator #(.width(2)) comparator_7 (.a(MemAddress[1:0]), .b(2'b11), .eq(Ob11));  // open: gt, lt
  Multiplexer #(.select(3), .width(32)) multiplexer_1 (
    .in0({{24{1'b0}}, DataFromReg[7:0]}), .in1({{16{1'b0}}, DataFromReg[7:0], {8{1'b0}}}),
    .in2({{8{1'b0}}, DataFromReg[7:0], {16{1'b0}}}), .in3({DataFromReg[7:0], {24{1'b0}}}),
    .in4({{16{1'b0}}, DataFromReg[15:0]}), .in5({DataFromReg[15:0], {16{1'b0}}}), .in6(DataFromReg),
    .out(DataToMem), .sel(index));  // open: in7
  Multiplexer #(.select(3), .width(4)) multiplexer_2 (
    .in0(4'b0001), .in1(4'b0010), .in2(4'b0100), .in3(4'b1000), .in4(4'b0011), .in5(4'b1100), .in6(4'b1111),
    .out(multiplexer_2_out), .sel(index));  // open: in7
  Multiplexer #(.width(4)) multiplexer_3 (.in0(4'b0000), .in1(multiplexer_2_out), .out(MemWriteMask), .sel(MemWEn));

  // Other names for the same wires on the sheet: DataFromReg_7_0[7:0] = DataFromReg[7:0];
  //   DataFromReg_15_0[15:0] = DataFromReg[15:0]; DataFromReg_15_8[7:0] = DataFromReg[15:8];
  //   DataFromReg_23_16[7:0] = DataFromReg[23:16]; DataFromReg_31_16[15:0] = DataFromReg[31:16];
  //   DataFromReg_31_24[7:0] = DataFromReg[31:24]; funct3[2:0] = Instruction[14:12]; Obxx[1:0] = MemAddress[1:0]

  // Notes on the sheet:
  //   INPUTS to your circuit
  //   Main
  //   DON'T CHANGE THE LOCATIONS OF THE INPUTS AND OUTPUTS!
  //   OUTPUT from your circuit
endmodule
