// Logisim project regfile.circ as structural Verilog: 1 circuit, main circuit regfile
module regfile (
  input  [4:0] ReadIndex1,
  input  [4:0] ReadIndex2,
  input  [4:0] WriteIndex,
  input  [31:0] WriteData,
  input  RegWEn,
  input  clk,
  output [31:0] ra,
  output [31:0] sp,
  output [31:0] t0,
  output [31:0] t1,
  output [31:0] t2,
  output [31:0] s0,
  output [31:0] s1,
  output [31:0] a0,
  output [31:0] ReadData1,
  output [31:0] ReadData2
);

  wire WI_00, WI_01, WI_02, WI_03, WI_04, WI_05, WI_06, WI_07, WI_08, WI_09, WI_10, WI_11, WI_12, WI_13,
       WI_14, WI_15, WI_16, WI_17, WI_18, WI_19, WI_20, WI_21, WI_22, WI_23, WI_24, WI_25, WI_26, WI_27,
       WI_28, WI_29, WI_30, WI_31;
  wire [31:0] x0, x3, x4, x11, x12, x13, x14, x15, x16, x17, x18, x19, x20, x21, x22, x23, x24, x25, x26,
       x27, x28, x29, x30, x31;

  Register #(.width(32)) register_1 (.D({32{1'b0}}), .en(WI_00), .clk(clk), .Q(x0));  // open: clr
  Register #(.width(32)) register_2 (.D(WriteData), .en(WI_04), .clk(clk), .Q(x4));  // open: clr
  Register #(.width(32)) register_3 (.D(WriteData), .en(WI_08), .clk(clk), .Q(s0));  // open: clr
  Register #(.width(32)) register_4 (.D(WriteData), .en(WI_12), .clk(clk), .Q(x12));  // open: clr
  Register #(.width(32)) register_5 (.D(WriteData), .en(WI_16), .clk(clk), .Q(x16));  // open: clr
  Register #(.width(32)) register_6 (.D(WriteData), .en(WI_20), .clk(clk), .Q(x20));  // open: clr
  Register #(.width(32)) register_7 (.D(WriteData), .en(WI_24), .clk(clk), .Q(x24));  // open: clr
  Register #(.width(32)) register_8 (.D(WriteData), .en(WI_28), .clk(clk), .Q(x28));  // open: clr
  Register #(.width(32)) register_9 (.D(WriteData), .en(WI_01), .clk(clk), .Q(ra));  // open: clr
  Register #(.width(32)) register_10 (.D(WriteData), .en(WI_05), .clk(clk), .Q(t0));  // open: clr
  Register #(.width(32)) register_11 (.D(WriteData), .en(WI_09), .clk(clk), .Q(s1));  // open: clr
  Register #(.width(32)) register_12 (.D(WriteData), .en(WI_13), .clk(clk), .Q(x13));  // open: clr
  Register #(.width(32)) register_13 (.D(WriteData), .en(WI_17), .clk(clk), .Q(x17));  // open: clr
  Register #(.width(32)) register_14 (.D(WriteData), .en(WI_21), .clk(clk), .Q(x21));  // open: clr
  Register #(.width(32)) register_15 (.D(WriteData), .en(WI_25), .clk(clk), .Q(x25));  // open: clr
  Register #(.width(32)) register_16 (.D(WriteData), .en(WI_29), .clk(clk), .Q(x29));  // open: clr
  Register #(.width(32)) register_17 (.D(WriteData), .en(WI_02), .clk(clk), .Q(sp));  // open: clr
  Register #(.width(32)) register_18 (.D(WriteData), .en(WI_06), .clk(clk), .Q(t1));  // open: clr
  Register #(.width(32)) register_19 (.D(WriteData), .en(WI_10), .clk(clk), .Q(a0));  // open: clr
  Register #(.width(32)) register_20 (.D(WriteData), .en(WI_14), .clk(clk), .Q(x14));  // open: clr
  Register #(.width(32)) register_21 (.D(WriteData), .en(WI_18), .clk(clk), .Q(x18));  // open: clr
  Register #(.width(32)) register_22 (.D(WriteData), .en(WI_22), .clk(clk), .Q(x22));  // open: clr
  Register #(.width(32)) register_23 (.D(WriteData), .en(WI_26), .clk(clk), .Q(x26));  // open: clr
  Register #(.width(32)) register_24 (.D(WriteData), .en(WI_30), .clk(clk), .Q(x30));  // open: clr
  Register #(.width(32)) register_25 (.D(WriteData), .en(WI_03), .clk(clk), .Q(x3));  // open: clr
  Register #(.width(32)) register_26 (.D(WriteData), .en(WI_07), .clk(clk), .Q(t2));  // open: clr
  Register #(.width(32)) register_27 (.D(WriteData), .en(WI_11), .clk(clk), .Q(x11));  // open: clr
  Register #(.width(32)) register_28 (.D(WriteData), .en(WI_15), .clk(clk), .Q(x15));  // open: clr
  Register #(.width(32)) register_29 (.D(WriteData), .en(WI_19), .clk(clk), .Q(x19));  // open: clr
  Register #(.width(32)) register_30 (.D(WriteData), .en(WI_23), .clk(clk), .Q(x23));  // open: clr
  Register #(.width(32)) register_31 (.D(WriteData), .en(WI_27), .clk(clk), .Q(x27));  // open: clr
  Register #(.width(32)) register_32 (.D(WriteData), .en(WI_31), .clk(clk), .Q(x31));  // open: clr
  Demultiplexer #(.select(5)) demultiplexer_1 (
    .out0(WI_00), .out1(WI_01), .out2(WI_02), .out3(WI_03), .out4(WI_04), .out5(WI_05), .out6(WI_06),
    .out7(WI_07), .out8(WI_08), .out9(WI_09), .out10(WI_10), .out11(WI_11), .out12(WI_12), .out13(WI_13),
    .out14(WI_14), .out15(WI_15), .out16(WI_16), .out17(WI_17), .out18(WI_18), .out19(WI_19), .out20(WI_20),
    .out21(WI_21), .out22(WI_22), .out23(WI_23), .out24(WI_24), .out25(WI_25), .out26(WI_26), .out27(WI_27),
    .out28(WI_28), .out29(WI_29), .out30(WI_30), .out31(WI_31), .in(RegWEn), .sel(WriteIndex));
  Multiplexer #(.select(5), .width(32)) multiplexer_1 (
    .in0(x0), .in1(ra), .in2(sp), .in3(x3), .in4(x4), .in5(t0), .in6(t1), .in7(t2), .in8(s0), .in9(s1),
    .in10(a0), .in11(x11), .in12(x12), .in13(x13), .in14(x14), .in15(x15), .in16(x16), .in17(x17),
    .in18(x18), .in19(x19), .in20(x20), .in21(x21), .in22(x22), .in23(x23), .in24(x24), .in25(x25),
    .in26(x26), .in27(x27), .in28(x28), .in29(x29), .in30(x30), .in31(x31), .out(ReadData1), .sel(ReadIndex1));
  Multiplexer #(.select(5), .width(32)) multiplexer_2 (
    .in0(x0), .in1(ra), .in2(sp), .in3(x3), .in4(x4), .in5(t0), .in6(t1), .in7(t2), .in8(s0), .in9(s1),
    .in10(a0), .in11(x11), .in12(x12), .in13(x13), .in14(x14), .in15(x15), .in16(x16), .in17(x17),
    .in18(x18), .in19(x19), .in20(x20), .in21(x21), .in22(x22), .in23(x23), .in24(x24), .in25(x25),
    .in26(x26), .in27(x27), .in28(x28), .in29(x29), .in30(x30), .in31(x31), .out(ReadData2), .sel(ReadIndex2));

  // Other names for the same wires on the sheet: x1[31:0] = ra; x2[31:0] = sp; x5[31:0] = t0; x6[31:0] = t1;
  //   x7[31:0] = t2; x8[31:0] = s0; x9[31:0] = s1; x10[31:0] = a0

  // Notes on the sheet:
  //   INPUTS to your circuit
  //   rd1
  //   rd2
  //   DON'T CHANGE THE LOCATIONS OF THE INPUTS AND OUTPUTS!
  //   These are DEBUG/TEST outputs from your circuit.
  //   OUTPUTS from your circuit
endmodule
